# Fritzing sketch DisplayForces (saved by Fritzing 0.6.3b)
breadboards: 1

parts:
  Part1 = Triple_Axis_Accelerometer_Breakout___ADXL345
  Arduino2 = Arduino
  U2 = 74HC595 [package="DIP16 [THT]"]
  DI5 = 7-Segment LED Display [package=THT]  # not connected
  DI6 = 7-Segment LED Display [package=THT]
  DI7 = 7-Segment LED Display [package=THT]
  DI8 = 7-Segment LED Display [package=THT]  # not connected
  J7 = female pin header, 2 pins [form="♀ (female)"]
  J8 = female pin header, 2 pins [form="♀ (female)"]
  J9 = female pin header, 2 pins [form="♀ (female)"]
  J10 = female pin header, 2 pins [form="♀ (female)"]
  J11 = female pin header, 2 pins [form="♀ (female)"]
  J12 = female pin header, 2 pins [form="♀ (female)"]

nets:
  N1: Part1.connector14, Arduino2.3V3
  GND: Part1.connector15, Arduino2.GND, U2.GND, U2.OE
  N2: Part1.connector17, Arduino2.D7
  N3: Part1.connector18, Arduino2.D6
  N4: Part1.connector20, Arduino2.A1
  N5: Part1.connector21, Arduino2.A2
  N6: Part1.connector22, Arduino2.A3
  N7: Arduino2.D12, U2.SH_CP
  N8: Arduino2.D11, U2.DS
  N9: Arduino2.D8, U2.ST_CP
  N10: Arduino2.D5, DI7.commAnode#7, J10.pin2
  N11: Arduino2.D4, DI6.cathodeG, J11.pin1
  N12: Arduino2.D3, DI6.cathodeF, J12.pin2
  N13: Arduino2.D2, DI6.commAnode#2, J9.pin1
  +5V: Arduino2.+5V, U2.MR, U2.VCC
  N14: U2.Q1, DI7.commAnode#2, J7.pin2
  N15: U2.Q2, DI7.cathodeB, J11.pin2
  N16: U2.Q3, DI7.cathodeA, J10.pin1
  N17: U2.Q4, DI6.commAnode#7, J12.pin1
  N18: U2.Q5, DI6.cathodeE, J8.pin1
  N19: U2.Q6, DI6.cathodeD, J9.pin2
  N20: U2.Q7, DI7.cathodeDP, J8.pin2
  N21: U2.Q0, DI7.cathodeC, J7.pin1
