# Fritzing sketch DisplayGPS (saved by Fritzing 0.6.3b)
breadboards: 2

parts:
  Arduino1 = Arduino
  U1 = 74HC595 [package="DIP16 [THT]"]
  U2 = 74HC595 [package="DIP16 [THT]"]
  DI1 = 7-Segment LED Display [package=THT]
  DI2 = 7-Segment LED Display [package=THT]
  R1 = Resistor [tolerance=±5% resistance=20 package=THT]
  R2 = Resistor [tolerance=±5% resistance=20 package=THT]
  Part1 = GPS_LS20031

nets:
  N1: Arduino1.D12, U1.SH_CP, U2.SH_CP
  N2: Arduino1.D11, U1.DS
  N3: Arduino1.D8, U1.ST_CP, U2.ST_CP
  N4: Arduino1.D0RX, Part1.connector9
  N5: Arduino1.3V3, R1.Pin_0, R2.Pin_0, Part1.connector7
  VCC: Arduino1.+5V, U1.MR, U1.VCC, U2.MR, U2.VCC
  GND: Arduino1.GND, U1.GND, U1.OE, U2.GND, U2.OE, Part1.connector10
  N6: U1.Q1, DI1.cathodeG
  N7: U1.Q2, DI1.cathodeF
  N8: U1.Q3, DI1.cathodeE
  N9: U1.Q4, DI1.cathodeD
  N10: U1.Q5, DI1.cathodeC
  N11: U1.Q6, DI1.cathodeB
  N12: U1.Q7, DI1.cathodeA
  N13: U1.Q7', U2.DS
  N14: U1.Q0, DI1.cathodeDP
  N15: U2.Q1, DI2.cathodeG
  N16: U2.Q2, DI2.cathodeF
  N17: U2.Q3, DI2.cathodeE
  N18: U2.Q4, DI2.cathodeD
  N19: U2.Q5, DI2.cathodeC
  N20: U2.Q6, DI2.cathodeB
  N21: U2.Q7, DI2.cathodeA
  N22: U2.Q0, DI2.cathodeDP
  N23: DI1.commAnode#7, R1.Pin_1
  N24: DI2.commAnode#7, R2.Pin_1

notes:
  3.3V
  5V
