# Fritzing sketch GPSForces (saved by Fritzing 0.6.3b)
breadboards: 2

parts:
  Arduino1 = Arduino
  DI1 = 7-Segment LED Display [package=THT]
  DI2 = 7-Segment LED Display [package=THT]
  U1 = 74HC595 [package="DIP16 [THT]"]
  U2 = 74HC595 [package="DIP16 [THT]"]
  Part1 = GPS_LS20031
  Part2 = Triple_Axis_Accelerometer_Breakout___ADXL345
  U3 = 74HC595 [package="DIP16 [THT]"]
  DI3 = 7_Segment_LED_Display

nets:
  N1: Arduino1.D7, U1.SH_CP, U2.SH_CP, U3.SH_CP
  N2: Arduino1.D6, U1.DS
  N3: Arduino1.D5, U1.ST_CP, U2.ST_CP, U3.ST_CP
  N4: Arduino1.D3, Part2.connector18
  N5: Arduino1.D0RX, Part1.connector9
  N6: Arduino1.3V3, DI1.commAnode#7, DI2.commAnode#7, Part1.connector7, Part2.connector14
  VCC: Arduino1.+5V, U1.MR, U1.VCC, U2.MR, U2.VCC, U3.MR, U3.VCC
  GND: Arduino1.GND, U1.GND, U1.OE, U2.GND, U2.OE, Part1.connector10, Part1.connector11, Part2.connector15, U3.GND, U3.OE, DI3.connector7
  N7: Arduino1.A1, Part2.connector20
  N8: Arduino1.A2, Part2.connector21
  N9: Arduino1.A3, Part2.connector22
  N10: DI1.cathodeE, U1.Q3
  N11: DI1.cathodeD, U1.Q4
  N12: DI1.cathodeC, U1.Q5
  N13: DI1.cathodeDP, U1.Q0
  N14: DI1.cathodeB, U1.Q6
  N15: DI1.cathodeA, U1.Q7
  N16: DI1.cathodeF, U1.Q2
  N17: DI1.cathodeG, U1.Q1
  N18: DI2.cathodeE, U2.Q3
  N19: DI2.cathodeD, U2.Q4
  N20: DI2.cathodeC, U2.Q5
  N21: DI2.cathodeDP, U2.Q0
  N22: DI2.cathodeB, U2.Q6
  N23: DI2.cathodeA, U2.Q7
  N24: DI2.cathodeF, U2.Q2
  N25: DI2.cathodeG, U2.Q1
  N26: U1.Q7', U2.DS
  N27: U2.Q7', U3.DS
  N28: U3.Q1, DI3.connector9
  N29: U3.Q2, DI3.connector8
  N30: U3.Q3, DI3.connector0
  N31: U3.Q4, DI3.connector1
  N32: U3.Q5, DI3.connector3
  N33: U3.Q6, DI3.connector5
  N34: U3.Q7, DI3.connector6
  N35: U3.Q0, DI3.connector4

notes:
  common cathode
  (G's)
  Common Anode
  (Speed)
  Accelerometer
  GPS
