# Fritzing sketch Sketch (saved by Fritzing 0.6.3b)
breadboards: 1

parts:
  Thermistor-LM1 = LM35_Temperature_Sensor
  4_Digit_7_Segment_Display1 = 4Digit7Segment [part_number=GD5643C]
  Arduino1 = Arduino

nets:
  N1: Thermistor-LM1.connector0, Arduino1.+5V
  N2: Thermistor-LM1.connector1, Arduino1.A0
  N3: Thermistor-LM1.connector2, Arduino1.GND
  N4: 4_Digit_7_Segment_Display1.connector0, Arduino1.D1TX
  N5: 4_Digit_7_Segment_Display1.connector1, Arduino1.D2
  N6: 4_Digit_7_Segment_Display1.connector2, Arduino1.D3
  N7: 4_Digit_7_Segment_Display1.connector3, Arduino1.D4
  N8: 4_Digit_7_Segment_Display1.connector4, Arduino1.D5
  N9: 4_Digit_7_Segment_Display1.connector5, Arduino1.D6
  N10: 4_Digit_7_Segment_Display1.connector6, Arduino1.D7
  N11: 4_Digit_7_Segment_Display1.connector7, Arduino1.D8
  N12: 4_Digit_7_Segment_Display1.connector8, Arduino1.D9
  N13: 4_Digit_7_Segment_Display1.connector9, Arduino1.D10
  N14: 4_Digit_7_Segment_Display1.connector10, Arduino1.D11
  N15: 4_Digit_7_Segment_Display1.connector11, Arduino1.D12
