# Fritzing sketch Sketch (saved by Fritzing 0.6.3b)
breadboards: 1

parts:
  Arduino1 = Arduino
  R1 = Resistor [tolerance=±5% resistance=220 package=THT]
  DI3 = 7_Segment_LED_Display

nets:
  N1: Arduino1.D9, DI3.connector4
  N2: Arduino1.D8, DI3.connector9
  N3: Arduino1.D7, DI3.connector8
  N4: Arduino1.D6, DI3.connector0
  N5: Arduino1.D5, DI3.connector1
  N6: Arduino1.D4, DI3.connector3
  N7: Arduino1.D3, DI3.connector5
  N8: Arduino1.D2, DI3.connector6
  N9: Arduino1.3V3, R1.Pin_1
  N10: R1.Pin_0, DI3.connector2
