# Fritzing sketch Sketch (saved by Fritzing 0.6.3b)

parts:
  4Dig7Seg1 = 4Dig7Seg
  Arduino1 = Arduino

nets:
  N1: 4Dig7Seg1.connector1, Arduino1.D6
  N2: 4Dig7Seg1.connector2, Arduino1.D5
  N3: 4Dig7Seg1.connector3, Arduino1.D4
  N4: 4Dig7Seg1.connector4, Arduino1.D3
  N5: 4Dig7Seg1.connector5, Arduino1.D2
  N6: 4Dig7Seg1.connector6, Arduino1.D1TX
  N7: 4Dig7Seg1.connector7, Arduino1.D7
  N8: 4Dig7Seg1.connector8, Arduino1.D8
  N9: 4Dig7Seg1.connector9, Arduino1.D9
  N10: 4Dig7Seg1.connector10, Arduino1.D10
  N11: 4Dig7Seg1.connector11, Arduino1.D11
  N12: 4Dig7Seg1.connector12, Arduino1.D12
