# Fritzing sketch NumCounter4DigShiftRegister (saved by Fritzing 0.6.3b)
breadboards: 1

parts:
  U1 = 74HC595 [package="DIP16 [THT]"]
  Arduino1 = Arduino
  DI1 = 7-Segment LED Display [package=THT]  # not connected
  DI2 = 7-Segment LED Display [package=THT]  # not connected
  DI3 = 7-Segment LED Display [package=THT]  # not connected
  DI4 = 7-Segment LED Display [package=THT]  # not connected
  J1 = female pin header, 2 pins [form="♀ (female)"]
  J2 = female pin header, 2 pins [form="♀ (female)"]
  J3 = female pin header, 2 pins [form="♀ (female)"]
  J4 = female pin header, 2 pins [form="♀ (female)"]
  J5 = female pin header, 2 pins [form="♀ (female)"]
  J6 = female pin header, 2 pins [form="♀ (female)"]

nets:
  N1: U1.Q1, J1.pin2
  N2: U1.Q2, J5.pin2
  N3: U1.Q3, J4.pin1
  N4: U1.Q4, J6.pin1
  N5: U1.Q5, J2.pin1
  N6: U1.Q6, J3.pin2
  N7: U1.Q7, J2.pin2
  GND: U1.GND, U1.OE, Arduino1.GND
  VCC: U1.MR, U1.VCC, Arduino1.+5V
  N8: U1.SH_CP, Arduino1.D12
  N9: U1.ST_CP, Arduino1.D8
  N10: U1.DS, Arduino1.D11
  N11: U1.Q0, J1.pin1
  N12: Arduino1.D5, J4.pin2
  N13: Arduino1.D4, J5.pin1
  N14: Arduino1.D3, J6.pin2
  N15: Arduino1.D2, J3.pin1
