# Fritzing sketch Sketch (saved by Fritzing 0.6.3b)
breadboards: 1

parts:
  U1 = 74HC595 [package="DIP16 [THT]"]
  Arduino1 = Arduino
  DI1 = 7-Segment LED Display [package=THT]

nets:
  N1: U1.Q1, DI1.cathodeB
  N2: U1.Q2, DI1.cathodeC
  N3: U1.Q3, DI1.cathodeD
  N4: U1.Q4, DI1.cathodeE
  N5: U1.Q5, DI1.cathodeF
  N6: U1.Q6, DI1.cathodeG
  N7: U1.Q7, DI1.cathodeDP
  GND: U1.GND, U1.OE, Arduino1.GND
  VCC: U1.MR, U1.VCC, Arduino1.+5V
  N8: U1.SH_CP, Arduino1.D12
  N9: U1.ST_CP, Arduino1.D8
  N10: U1.DS, Arduino1.D11
  N11: U1.Q0, DI1.cathodeA
