# Fritzing sketch Sketch (saved by Fritzing 0.6.3b)
breadboards: 1

parts:
  Arduino1 = Arduino
  DI1 = 7-Segment LED Display [package=THT]
  R1 = Resistor [tolerance=±5% resistance=220 package=THT]

nets:
  N1: Arduino1.D2, DI1.cathodeDP
  N2: Arduino1.3V3, R1.Pin_0
  N3: DI1.commAnode#2, R1.Pin_1
